# Fritzing sketch circuit (saved by Fritzing 0.9.2b)
breadboards: 1

parts:
  Q1 = NPN-Transistor [package="TO92 [THT]"]
  VCC1 = Battery block 9V
  Raspberry_Pi1 = Raspberry Pi 2
  R1 = Resistor [tolerance=±5% resistance=2.2k package=THT]
  M1 = DC Motor
  Q2 = NPN-Transistor [package="TO92 [THT]"]
  R2 = Resistor [tolerance=±5% resistance=2.2k package=THT]
  U2 = RELAY [package=relay-t9a]
  U1 = 941H-2C-5D [package=relay-5v]
  S1 = Pushbutton [package=THT]
  S2 = Pushbutton [package=THT]

nets:
  N1: Q1.E, U1.16
  N2: Q1.B, R1.Pin_1
  N3: Q1.C, U2.NO
  GND: VCC1.-, Raspberry_Pi1.GND, U2.COIL1, U1.1, U1.6, U1.9
  N4: VCC1.+, Q2.C, U2.MAIN, U1.8, U1.11
  N5: Raspberry_Pi1.GPIO4, S2.leg0
  N6: Raspberry_Pi1.GPIO17, S1.leg0
  N7: Raspberry_Pi1.3V3, S1.leg1, S2.leg1
  N8: Raspberry_Pi1.GPIO24, R2.Pin_0
  N9: Raspberry_Pi1.GPIO23, R1.Pin_0
  N10: M1.pin_1, U1.13
  N11: M1.pin_2, U1.4
  N12: Q2.E, U2.COIL2
  N13: Q2.B, R2.Pin_1

custom parts:
  941H-2C-5D: DPDT Relay - 2 Form C
